# Fritzing sketch schematic (saved by Fritzing 0.9.3b)
breadboards: 1

parts:
  2N7000_1 = MOSFET-NCHANNEL [package=sot323]
  Motor_1 = Vibration Motor- ROB-08449 [package=vibe-motor-10mm]
  Battery = LIPO-110mAh [package=lipo-110]
  2N7000_2 = MOSFET-NCHANNEL [package=sot323]
  Motor_2 = Vibration Motor- ROB-08449 [package=vibe-motor-10mm]
  2N7000_3 = MOSFET-NCHANNEL [package=sot323]
  Motor_3 = Vibration Motor- ROB-08449 [package=vibe-motor-10mm]
  MCU = Adafruit HUZZAH32 ESP32 Feather [part_number="Adafruit #3405"]

nets:
  N1: 2N7000_1.G, MCU.IO12_A11
  N2: 2N7000_1.S, Battery.+, 2N7000_2.S, 2N7000_3.S, MCU.GND
  N3: 2N7000_1.D, Motor_1.-
  N4: Motor_1.+, Battery.-, Motor_2.+, Motor_3.+, MCU.VBAT
  N5: 2N7000_2.G, MCU.IO14_A6
  N6: 2N7000_2.D, Motor_2.-
  N7: 2N7000_3.G, MCU.IO33_A9
  N8: 2N7000_3.D, Motor_3.-
